// Logisim project schematic.circ as structural Verilog
module fulladder (
  input  CIN,
  input  A,
  input  B,
  output SUM,
  output COUT
);

  wire and_1_out, and_2_out, xor_1_out;

  xor xor_1 (xor_1_out, A, B);
  and and_1 (and_1_out, B, A);
  xor xor_2 (SUM, CIN, xor_1_out);
  and and_2 (and_2_out, CIN, xor_1_out);
  or or_1 (COUT, and_2_out, and_1_out);
endmodule

module FA_16 (
  input  [15:0] A,
  input  CIN,
  input  [15:0] B,
  output [15:0] SUM,
  output COUT
);

  wire fa_4_1_cout, fa_4_2_cout, fa_4_3_cout;

  FA_4 fa_4_1 (.A(A[3:0]), .B(B[3:0]), .CIN(CIN), .COUT(fa_4_1_cout), .SUM(SUM[3:0]));
  FA_4 fa_4_2 (.A(A[7:4]), .B(B[7:4]), .CIN(fa_4_1_cout), .COUT(fa_4_2_cout), .SUM(SUM[7:4]));
  FA_4 fa_4_3 (.A(A[11:8]), .B(B[11:8]), .CIN(fa_4_2_cout), .COUT(fa_4_3_cout), .SUM(SUM[11:8]));
  FA_4 fa_4_4 (.A(A[15:12]), .B(B[15:12]), .CIN(fa_4_3_cout), .COUT(COUT), .SUM(SUM[15:12]));
endmodule

module FA_4 (
  input  [3:0] A,
  input  CIN,
  input  [3:0] B,
  output [3:0] SUM,
  output COUT
);

  wire fulladder_1_cout, fulladder_2_cout, fulladder_3_cout;

  fulladder fulladder_1 (.A(A[0]), .B(B[0]), .CIN(CIN), .COUT(fulladder_1_cout), .SUM(SUM[0]));
  fulladder fulladder_2 (.A(A[1]), .B(B[1]), .CIN(fulladder_1_cout), .COUT(fulladder_2_cout), .SUM(SUM[1]));
  fulladder fulladder_3 (.A(A[2]), .B(B[2]), .CIN(fulladder_2_cout), .COUT(fulladder_3_cout), .SUM(SUM[2]));
  fulladder fulladder_4 (.A(A[3]), .B(B[3]), .CIN(fulladder_3_cout), .COUT(COUT), .SUM(SUM[3]));
endmodule

module ALU (
  input  [15:0] A,
  input  [15:0] B
);

  FA_16 fa_16_1 ();  // open: B, A, CIN, COUT, SUM
endmodule
